# Fritzing sketch Circuit (saved by Fritzing 0.9.10b)
breadboards: 1

parts:
  Mod1 = Raspberry Pi Pico
  A1 = gy-sgp30
  Composant2 = Barometric Pressure Sensor - BMP180 Breakout (GY-68)
  A2 = PMS5003

nets:
  N1: Mod1.pin_1, A1.Pin_3, Composant2.SDA
  N2: Mod1.pin_2, A1.Pin_4, Composant2.SCL
  N3: Mod1.pin_3, Mod1.pin_8, Mod1.pin_13, Mod1.pin_18, Mod1.pin_23, Mod1.pin_28, Mod1.pin_33, Mod1.pin_38, A1.Pin_2, Composant2.GND, A2.Pin_2
  N4: Mod1.pin_4, A2.Pin_6
  N5: Mod1.pin_5, A2.Pin_3
  N6: Mod1.pin_21, A2.Pin_4
  N7: Mod1.pin_22, A2.Pin_5
  N8: Mod1.pin_40, A1.Pin_1, Composant2.VDD, A2.Pin_1

custom parts:
  Raspberry Pi Pico: Raspberry Pi Pico. Based around the RP2040 microcontroller the Pico is a low cost microcontroller device bringing Raspberry Pi quality, cost, and easy of use to the microcontroller space. Jan 2021, Split part in to two versions: tht (this one) and SMD. This one will drill holes for a .1 in header in pcb to allow plugging in the module as well as providing pads to solder the module to the top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
  gy-sgp30: GY-SGP30 Gas Sensor Chip Module Air Quality TVOC ECO2 Carbon Dioxide CO2 IIC I2C 3.3V 5V SGP30 Measurement Detector Formaldehyde.
  Barometric Pressure Sensor - BMP180 Breakout (GY-68): This is a simple breakout board for the BMP180, a high-precision, low-power barometric pressure sensor made by Bosch Sensortec. The range of measurement is from 300hPa to 1100hPa. The sensor can be supplied with voltage ranging from 1.8V to 3.6V. Operating temperature range is -40 to +85 °C. This particular breakout board (or perhaps the configuration) is produced by Shenzhen Keep Power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
  PMS5003: PMS5003 is a kind of digital and universal particle concentration sensor, which can be used to obtain the number of suspended particles in the air.
