# Fritzing sketch Circuit (saved by Fritzing 0.9.10b)
breadboards: 1

parts:
  A1 = gy-sgp30
  Composant2 = Barometric Pressure Sensor - BMP180 Breakout (GY-68)
  A2 = PMS5003
  Mod1 = Raspberry Pi 4B

nets:
  VDD: A1.Pin_1, Composant2.VDD, A2.Pin_1, Mod1.5V
  GND: A1.Pin_2, Composant2.GND, A2.Pin_2, Mod1.GND
  N1: A1.Pin_3, Composant2.SDA
  N2: A1.Pin_4, Composant2.SCL
  N3: A2.Pin_3, Mod1.GPIO3
  N4: A2.Pin_4, Mod1.GPIO14
  N5: A2.Pin_5, Mod1.GPIO15
  N6: A2.Pin_6, Mod1.GPIO2

custom parts:
  gy-sgp30: GY-SGP30 Gas Sensor Chip Module Air Quality TVOC ECO2 Carbon Dioxide CO2 IIC I2C 3.3V 5V SGP30 Measurement Detector Formaldehyde.
  Barometric Pressure Sensor - BMP180 Breakout (GY-68): This is a simple breakout board for the BMP180, a high-precision, low-power barometric pressure sensor made by Bosch Sensortec. The range of measurement is from 300hPa to 1100hPa. The sensor can be supplied with voltage ranging from 1.8V to 3.6V. Operating temperature range is -40 to +85 °C. This particular breakout board (or perhaps the configuration) is produced by Shenzhen Keep Power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
  PMS5003: PMS5003 is a kind of digital and universal particle concentration sensor, which can be used to obtain the number of suspended particles in the air.
